# Fritzing sketch OhaEnergyUseLog (saved by Fritzing 0.9.3b)
circuit board: 19.05cm x 9.05cm
breadboards: 1

parts:
  R1 = Resistor [tolerance=±5% resistance=33 package=THT]
  J1 = female pin header, 2 pins [form="♀ (female)"]
  R2 = Resistor [tolerance=±5% resistance=33 package=THT]
  J2 = female pin header, 2 pins [form="♀ (female)"]
  R3 = Resistor [tolerance=±5% resistance=33 package=THT]
  J3 = female pin header, 2 pins [form="♀ (female)"]
  D11 = Rectifier Diode [part_number=1N4001 package="300 mil [THT]"]
  D12 = Rectifier Diode [part_number=1N4001 package="300 mil [THT]"]
  D21 = Rectifier Diode [part_number=1N4001 package="300 mil [THT]"]
  D22 = Rectifier Diode [part_number=1N4001 package="300 mil [THT]"]
  D23 = Rectifier Diode [part_number=1N4001 package="300 mil [THT]"]
  D24 = Rectifier Diode [part_number=1N4001 package="300 mil [THT]"]
  D31 = Rectifier Diode [part_number=1N4001 package="300 mil [THT]"]
  D33 = Rectifier Diode [part_number=1N4001 package="300 mil [THT]"]
  D32 = Rectifier Diode [part_number=1N4001 package="300 mil [THT]"]
  D34 = Rectifier Diode [part_number=1N4001 package="300 mil [THT]"]
  J4_-_AC_P8 = female pin header, 3 pins [form="♀ (female)"]
  D14 = Rectifier Diode [part_number=1N4001 package="300 mil [THT]"]
  D13 = Rectifier Diode [part_number=1N4001 package="300 mil [THT]"]
  Ams1117_3_3V = V_REG_LD1117VXX [package=78xxl]
  ESP8266-2 = female pin header, 4 pins [form="♀ (female)"]
  ESP8266-1 = female pin header, 4 pins [form="♀ (female)"]
  Cooler_5V = female pin header, 2 pins [form="♀ (female)"]
  Cooler_5V1 = female pin header, 2 pins [form="♀ (female)"]
  C-450uf = Electrolytic Capacitor [capacitance=1µF voltage=16V package="100 mil [THT, electrolytic]"]
  C-100uF = Electrolytic Capacitor [capacitance=1pF voltage=16V package="100 mil [THT, electrolytic]"]
  LED_-_IO5 = LED - 5mm [color="Green (555nm)" package="5 mm [THT]"]
  R5-330 = Resistor [tolerance=±5% resistance=330 package=THT]
  RoboCore_-_BlackBoard_V1_0 = Arduino Uno (Rev3)
  ESP8266_-_CL = Logic Level Converter
  MicroSD1 = female pin header, 6 pins [form="♀ (female)"]
  Pad_-_GND = Pad [width=3.7675255555555553 height=2.2246437227722802 connect=center]

nets (from the pcb view):
  N1: R1.Pin_0, D11.cathode, D12.cathode, RoboCore_-_BlackBoard_V1_0.A0
  GND: R1.Pin_1, R2.Pin_1, R3.Pin_1, D23.anode, D24.anode, D33.anode, D34.anode, J4_-_AC_P8.pin1, D14.anode, D13.anode, Ams1117_3_3V.GND, ESP8266-2.pin4, Cooler_5V.pin2, Cooler_5V1.pin1, C-450uf.-, C-100uF.-, R5-330.Pin_1, RoboCore_-_BlackBoard_V1_0.GND, ESP8266_-_CL.GND, MicroSD1.pin1, Pad_-_GND.pad
  N2: J1.pin1, D11.anode, D13.cathode
  N3: J1.pin2, D12.anode, D14.cathode
  N4: R2.Pin_0, D21.cathode, D22.cathode, RoboCore_-_BlackBoard_V1_0.A1
  N5: J2.pin1, D21.anode, D23.cathode
  N6: J2.pin2, D22.anode, D24.cathode
  N7: R3.Pin_0, D31.cathode, D32.cathode, RoboCore_-_BlackBoard_V1_0.A2
  N8: J3.pin1, D31.anode, D33.cathode
  N9: J3.pin2, D32.anode, D34.cathode
  N10: J4_-_AC_P8.pin2, RoboCore_-_BlackBoard_V1_0.A5/SCL
  N11: J4_-_AC_P8.pin3, RoboCore_-_BlackBoard_V1_0.5V, ESP8266_-_CL.HV, MicroSD1.pin2
  N12: Ams1117_3_3V.OUT, ESP8266-1.pin1, C-100uF.+, ESP8266_-_CL.LV
  N13: Ams1117_3_3V.IN, C-450uf.+, RoboCore_-_BlackBoard_V1_0.VIN
  N14: ESP8266-2.pin1, ESP8266_-_CL.RX_LV
  N15: ESP8266-1.pin3, ESP8266_-_CL.RX2_LV
  N16: ESP8266-1.pin4, ESP8266_-_CL.TX_LV
  N17: Cooler_5V.pin1, Cooler_5V1.pin2, RoboCore_-_BlackBoard_V1_0.D9_PWM
  N18: LED_-_IO5.cathode, RoboCore_-_BlackBoard_V1_0.D5_PWM
  N19: LED_-_IO5.anode, R5-330.Pin_0
  N20: RoboCore_-_BlackBoard_V1_0.D10_PWM/SS, MicroSD1.pin6
  N21: RoboCore_-_BlackBoard_V1_0.D11_PWM/MOSI, MicroSD1.pin4
  N22: RoboCore_-_BlackBoard_V1_0.D12/MISO, MicroSD1.pin3
  N23: RoboCore_-_BlackBoard_V1_0.D13/SCK, MicroSD1.pin5
  N24: RoboCore_-_BlackBoard_V1_0.D2, ESP8266_-_CL.TX_HV
  N25: RoboCore_-_BlackBoard_V1_0.D3_PWM, ESP8266_-_CL.RX_HV
  N26: RoboCore_-_BlackBoard_V1_0.D4, ESP8266_-_CL.RX2_HV

notes:
  OHA 1.0 24/06/16

custom parts:
  Logic Level Converter: Description: If you've ever tried to connect a 3.3V device to a 5V system, you know what a challenge it can be. The SparkFun logic level converter is a small device that safely steps down 5V signals to 3.3V and steps up 3.3V to 5V. This level converter also works with 2.8V and 1.8V devices. Each level converter has the capability of converting 4 pins on the high side to 4 pins on the low side.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
